// Logisim project Invalid IC.circ as structural Verilog: 1 circuit, main circuit main
module main (
  input  _1__1A,
  input  _14__Vcc,
  input  _2__1B,
  input  _13__4B,
  input  _12__4A,
  input  _4__2A,
  input  _5__2B,
  input  _10__3B,
  input  _9__3A,
  input  _7__GND,
  output _3__1Y,
  output _11__4Y,
  output _6__2Y,
  output _8__3Y
);

  nand nand_1 (_3__1Y, _2__1B, _1__1A);
  nand nand_2 (_6__2Y, _5__2B, _4__2A);
  and and_1 (_11__4Y, _13__4B, _12__4A);
  and and_2 (_8__3Y, _10__3B, _9__3A);
endmodule
