// Logisim project Lido.circ as structural Verilog: 1 circuit, main circuit main
module main (
  input  Reset,
  input  Enable
);

  wire clock_1_out, main_2_not_valid, main_3_q0, main_3_q1, main_3_q2, main_3_q3, main_4_c0, main_4_c1,
       main_4_found, main_5_oc1, main_5_oco, main_5_ofound, n7400_2_p3, n7400_2_p6, n7400_2_p11, n7400_2_p14,
       n74161_1_p3, n74161_1_p6, n74161_1_p7, n74161_1_p8, not_1_out;

  // Invalid_IC_main main_1: pin names not known
  Clock clock_1 (.out(clock_1_out));
  // _7400 7400_1: pin names not known
  // _7408 7408_1: pin names not known
  // _74161 74161_1: pin names not known; wires that end beside it: Reset, clock_1_out, n74161_1_p3, 1'b0, 1'b1, n74161_1_p6, n74161_1_p7, n74161_1_p8, 1'b1
  // _7432 7432_1: pin names not known
  // _7486 7486_1: pin names not known
  // _7400 7400_2: pin names not known; wires that end beside it: n74161_1_p6, n74161_1_p7, n7400_2_p3, n74161_1_p6, n74161_1_p7, n7400_2_p6, 1'b0, 1'b1, n74161_1_p6, n74161_1_p7, n7400_2_p11, n74161_1_p6, n74161_1_p7, n7400_2_p14
  check_gates_main main_2 (
    .Yo(n7400_2_p11), .Y1(n7400_2_p14), .Y2(n7400_2_p6), .Y3(n7400_2_p3), .Not_Valid(main_2_not_valid));
  LED Found (.in(main_5_ofound));
  not not_1 (not_1_out, main_5_ofound);
  LED Not_Found (.in(not_1_out));
  Register_main main_3 (
    .DSA(n7400_2_p11), .DSB(n7400_2_p11), .CP(clock_1_out), .En(n74161_1_p3), .nMR(Reset), .Q0(main_3_q0),
    .Q1(main_3_q1), .Q2(main_3_q2), .Q3(main_3_q3));  // open: Q4, Q5, Q6, Q7
  project_output_main main_4 (
    .y0(main_3_q3), .y1(main_3_q2), .y2(main_3_q1), .y3(main_3_q0), .Checker(main_2_not_valid),
    .C1(main_4_c1), .C0(main_4_c0), .Found(main_4_found));
  Terminate_block_main main_5 (
    .Found(main_4_found), .C1(main_4_c1), .Co(main_4_c0), .Bit3(n74161_1_p8), .Enable(Enable),
    .OFound(main_5_ofound), .OC1(main_5_oc1), .OCo(main_5_oco), .OEnable(n74161_1_p3));
  LED C0 (.in(main_5_oco));
  LED C1 (.in(main_5_oc1));

  // Notes on the sheet:
  //   _____
endmodule
