// Logisim project Register.circ as structural Verilog: 1 circuit, main circuit main
module main (
  input  DSA,
  input  DSB,
  input  CP,
  input  En,
  input  nMR,
  output Q0,
  output Q1,
  output Q2,
  output Q3,
  output Q4,
  output Q5,
  output Q6,
  output Q7
);

  wire and_1_out, and_2_out, buffer_1_out, not_1_out;

  buf buffer_1 (buffer_1_out, CP);
  and and_1 (and_1_out, DSA, DSB);
  and and_2 (and_2_out, buffer_1_out, En);
  not not_1 (not_1_out, nMR);
  D_Flip_Flop d_ff_1 (.clk(and_2_out), .D(and_1_out), .Q(Q0), .reset(not_1_out));  // open: Qn, preset, en
  D_Flip_Flop d_ff_2 (.clk(and_2_out), .D(Q0), .Q(Q1), .reset(not_1_out));  // open: Qn, preset, en
  D_Flip_Flop d_ff_3 (.clk(and_2_out), .D(Q1), .Q(Q2), .reset(not_1_out));  // open: Qn, preset, en
  D_Flip_Flop d_ff_4 (.clk(and_2_out), .D(Q2), .Q(Q3), .reset(not_1_out));  // open: Qn, preset, en
  D_Flip_Flop d_ff_5 (.clk(and_2_out), .D(Q3), .Q(Q4), .reset(not_1_out));  // open: Qn, preset, en
  D_Flip_Flop d_ff_6 (.clk(and_2_out), .D(Q4), .Q(Q5), .reset(not_1_out));  // open: Qn, preset, en
  D_Flip_Flop d_ff_7 (.clk(and_2_out), .D(Q5), .Q(Q6), .reset(not_1_out));  // open: Qn, preset, en
  D_Flip_Flop d_ff_8 (.clk(and_2_out), .D(Q6), .Q(Q7), .reset(not_1_out));  // open: Qn, preset, en
endmodule
