// Logisim project Terminate block.circ as structural Verilog: 1 circuit, main circuit main
module main (
  input  Found,
  input  C1,
  input  Co,
  input  Bit3,
  input  Enable,
  output OFound,
  output OC1,
  output OCo,
  output OEnable
);

  wire not_1_out;

  and and_1 (OFound, Found, Bit3);
  and and_2 (OC1, C1, Bit3);
  and and_3 (OCo, Co, Bit3);
  not not_1 (not_1_out, Bit3);
  and and_4 (OEnable, not_1_out, Enable);
endmodule
