// Logisim project check gates.circ as structural Verilog: 1 circuit, main circuit main
module main (
  input  Yo,
  input  Y1,
  input  Y2,
  input  Y3,
  output Not_Valid
);

  wire or_1_out, xor_1_out, xor_2_out, xor_3_out;

  xor xor_1 (xor_1_out, Yo, Y1);
  xor xor_2 (xor_2_out, Y2, Y3);
  xor xor_3 (xor_3_out, Yo, Y2);
  or or_1 (or_1_out, xor_1_out, xor_2_out);
  or or_2 (Not_Valid, or_1_out, xor_3_out);
endmodule
