// Logisim project project output.circ as structural Verilog: 1 circuit, main circuit main
module main (
  input  y0,
  input  y1,
  input  y2,
  input  y3,
  input  Checker,
  output C1,
  output C0,
  output Found
);

  wire and_1_out, and_2_out, and_3_out, not_1_out, or_2_out, or_3_out, or_4_out, xor_1_out;

  not not_1 (not_1_out, y2);
  and and_1 (and_1_out, y2, y3);
  and and_2 (and_2_out, y0, y3);
  and and_3 (and_3_out, C1, not_1_out);
  xor xor_1 (xor_1_out, y2, y1);
  or or_1 (C0, and_1_out, y0);
  not not_2 (C1, y3);
  or or_2 (or_2_out, and_2_out, and_3_out);
  or or_3 (or_3_out, or_2_out, xor_1_out);
  or or_4 (or_4_out, or_3_out, Checker);
  not not_3 (Found, or_4_out);
endmodule
